// Logisim project Project_2207099.circ as structural Verilog: 33 circuits, main circuit main
module CPU (
  input  CLR
);

  wire a1, a2, a3, a4, b1, b2, b3, Bz, c1, c2, CLK, clock_1_out, d1, d2, f1, f2, I, inc_dec, j_k_ff_1_q,
       LOAD_A, LOAD_B, LOAD_PC, not_1_out, not_2_out, or_4_out, R, S, W;
  wire [1:0] n16x1_mux_1_sbit, n16x1_mux_2_sbit;
  wire [3:0] ir;
  wire [4:0] Mar, multiplexer_4_out, multiplexer_5_out;
  wire [21:0] A, B, controlled_buffer_1_out, main_2_output, mdata, multiplexer_1_out, multiplexer_2_out,
       multiplexer_3_out, pcdata, Res;

  Clock clock_1 (.out(clock_1_out));
  not not_1 (not_1_out, S);
  _16x1_MUX u_16x1_mux_1 (.in_1(ir), .sbit(n16x1_mux_1_sbit));
  Multiplexer #(.width(22), .enable("false")) multiplexer_1 (
    .in0(B), .in1(22'h1), .out(multiplexer_1_out), .sel(inc_dec));
  and and_1 (CLK, clock_1_out, not_1_out);
  Multiplexer #(.select(2), .width(22), .enable("false")) multiplexer_2 (
    .in0({pcdata[21:20], 4'b0101, pcdata[15:0]}), .in1(mdata), .in2(A), .out(multiplexer_2_out), .sel({b1, R}));  // open: in3
  main main_1 (
    .Control(n16x1_mux_1_sbit), .A(A), .B(multiplexer_1_out), .Output(Res));  // open: Negative, Zero, Overflow, Carry
  J_K_Flip_Flop j_k_ff_1 (.J(f1), .clk(clock_1_out), .K(f2), .Q(j_k_ff_1_q), .reset(CLR));  // open: Qn, preset, en
  IR ir_1 (.Load(I), .clk(clock_1_out), .In(B[19:16]), .CLR(CLR), .Out(ir));
  // Probe on ir
  or or_1 (LOAD_A, a1, a2, a3, a4);
  MBR mbr_1 (.Counter(b2), .Load(LOAD_B), .IN(controlled_buffer_1_out), .CLK(CLK), .CLR(CLR), .OUT(B));
  _16x1_MUX u_16x1_mux_2 (.in_1(ir), .sbit(n16x1_mux_2_sbit));
  assign controlled_buffer_1_out = not_2_out ? multiplexer_2_out : 22'bz;  // Controlled_Buffer controlled_buffer_1
  assign controlled_buffer_1_out = inc_dec ? main_2_output : 22'bz;  // Controlled_Buffer controlled_buffer_2
  not not_2 (not_2_out, inc_dec);
  // Probe on B[4:0]
  // Probe on B
  main main_2 (
    .Control(n16x1_mux_2_sbit), .A(B), .B(22'h1), .Output(main_2_output));  // open: Negative, Zero, Overflow, Carry
  RAM #(.addrWidth(5), .dataWidth(22), .bus("separate")) ram_1 (
    .addr(Mar), .din(B), .data(mdata), .str(W), .clk(CLK), .ld(R));  // open: sel, clr
  or or_2 (LOAD_B, b1, R, b3);
  Multiplexer #(.width(22), .enable("false")) multiplexer_3 (.in0(Res), .in1(B), .out(multiplexer_3_out), .sel(a3));
  Accumulator accumulator_1 (.Load(LOAD_A), .In(multiplexer_3_out), .CLk(CLK), .CLR(CLR), .Out(A));
  Control_Unit control_unit_1 (
    .F(j_k_ff_1_q), .IR(ir), .CLK(CLK), .CLR(CLR), .Bz(Bz), .R(R), .W(W), .a1(a1), .a2(a2), .a3(a3), .b1(b1),
    .b2(b2), .b3(b3), .c1(c1), .c2(c2), .d1(d1), .d2(d2), .I(I), .f1(f1), .f2(f2), .S(S), .a4(a4),
    .inc_dec(inc_dec));
  // Probe on A
  Zero zero_1 (.in_1(B), .Zero(Bz));
  or or_3 (LOAD_PC, c2, b3);
  // Probe on B[4:0]
  Multiplexer #(.width(5), .enable("false")) multiplexer_4 (.in0(Mar), .in1(B[4:0]), .out(multiplexer_4_out), .sel(c2));
  Multiplexer #(.width(5), .enable("false")) multiplexer_5 (
    .in0(pcdata[4:0]), .in1(B[4:0]), .out(multiplexer_5_out), .sel(d2));
  or or_4 (or_4_out, d1, d2);
  // Probe on multiplexer_5_out
  PC pc_1 (.Counter(c1), .Load(LOAD_PC), .IN(multiplexer_4_out), .CLk(CLK), .CLR(CLR), .OUT(pcdata[4:0]));
  // Probe on Mar
  // Probe on pcdata[4:0]
  MAR mar_1 (.Load(or_4_out), .In(multiplexer_5_out), .CLR(CLR), .CLk(CLK), .Out(Mar));
  // Probe on {pcdata[21:20], 4'b0101, pcdata[15:0]}

  // Other names for the same wires on the sheet: B_AD[4:0] = B[4:0]; B_OP[3:0] = B[19:16]; sbit[1:0] = {b1, R}

  // Notes on the sheet:
  //   2207099
endmodule

// ALU
module main (
  input  [1:0] Control,
  input  [21:0] A,
  input  [21:0] B,
  output [21:0] Output,
  output Negative,
  output Zero,
  output Overflow,
  output Carry
);

  wire n22_bit_parallel_adder_1_carry, n22_bit_parallel_adder_1_overflow, negative_1_c, not_1_out;
  wire [21:0] and_circuit_1_c, n22_bit_parallel_adder_1_output, or_circuit_1_c;

  // Probe on A
  // Probe on B
  not not_1 (not_1_out, Control[1]);
  _22_bit_Parallel_Adder u_22_bit_parallel_adder_1 (
    .in_1(Control[0]), .in_2(A), .in_3(B), .Output(n22_bit_parallel_adder_1_output),
    .Overflow(n22_bit_parallel_adder_1_overflow), .Carry(n22_bit_parallel_adder_1_carry));  // open: zero
  AND_Circuit and_circuit_1 (.A(A), .B(B), .C(and_circuit_1_c));
  OR_Circuit or_circuit_1 (.A(A), .B(B), .C(or_circuit_1_c));
  Multiplexer #(.select(2), .width(22), .enable("false")) multiplexer_1 (
    .in0(n22_bit_parallel_adder_1_output), .in1(n22_bit_parallel_adder_1_output), .in2(and_circuit_1_c),
    .in3(or_circuit_1_c), .out(Output), .sel(Control));
  and and_1 (Overflow, not_1_out, n22_bit_parallel_adder_1_overflow);
  and and_2 (Carry, not_1_out, n22_bit_parallel_adder_1_carry);
  Negative negative_1 (.in_1(Output), .C(negative_1_c));
  Zero zero_1 (.in_1(Output), .Zero(Zero));
  and and_3 (Negative, negative_1_c, not_1_out);
  // Probe on Output

  // Notes on the sheet:
  //   2207099
  //   10 - AND
  //   11 - OR
  //   00 - Adder
  //   01 - Subtractor
endmodule

// AND
module AND_Circuit (
  input  [21:0] A,
  input  [21:0] B,
  output [21:0] C
);

  assign C = A & B;  // AND_Gate and_1, 22 bits wide

  // Notes on the sheet:
  //   2207099
endmodule

// OR
module OR_Circuit (
  input  [21:0] A,
  input  [21:0] B,
  output [21:0] C
);

  assign C = A | B;  // OR_Gate or_1, 22 bits wide

  // Notes on the sheet:
  //   2207099
endmodule

module _1_bit_FA (
  input  A,
  input  B,
  input  C_IN,
  output SUM,
  output C_OUT
);

  wire and_1_out, and_2_out, xor_1_out;

  and and_1 (and_1_out, A, B);
  xor xor_1 (xor_1_out, A, B);
  xor xor_2 (SUM, xor_1_out, C_IN);
  and and_2 (and_2_out, xor_1_out, C_IN);
  or or_1 (C_OUT, and_2_out, and_1_out);

  // Notes on the sheet:
  //   2207099
endmodule

module _2_bit_CLAG (
  input  in_1,
  input  [1:0] in_2,
  input  [1:0] in_3,
  output C1,
  output C2
);

  wire and_1_out, and_2_out, and_3_out, G0_out, g1_out, P0_out, p1_out;

  xor P0 (P0_out, in_2[0], in_3[0]);
  xor p1 (p1_out, in_2[1], in_3[1]);
  and G0 (G0_out, in_2[0], in_3[0]);
  and g1 (g1_out, in_2[1], in_3[1]);
  and and_1 (and_1_out, in_1, P0_out);
  and and_2 (and_2_out, P0_out, p1_out, in_1);
  and and_3 (and_3_out, G0_out, p1_out);
  or or_1 (C1, and_1_out, G0_out);
  or or_2 (C2, and_2_out, and_3_out, g1_out);

  // Notes on the sheet:
  //   2207099
endmodule

// 4 CL
module _4_bit_CLAG (
  input  C0,
  input  [3:0] A,
  input  [3:0] B,
  output C1,
  output C2,
  output C3,
  output C4
);

  wire and_1_out, and_2_out, and_3_out, and_4_out, and_5_out, and_6_out, and_7_out, and_8_out, and_9_out,
       and_10_out, G0_out, G1_out, G2_out, G3_out, P0_out, P1_out, P2_out, P3_out;

  xor P0 (P0_out, A[0], B[0]);
  xor P1 (P1_out, A[1], B[1]);
  xor P2 (P2_out, A[2], B[2]);
  xor P3 (P3_out, A[3], B[3]);
  and G0 (G0_out, A[0], B[0]);
  and G1 (G1_out, A[1], B[1]);
  and G2 (G2_out, A[2], B[2]);
  and G3 (G3_out, A[3], B[3]);
  and and_1 (and_1_out, P0_out, C0);
  and and_2 (and_2_out, P0_out, P1_out, C0);
  and and_3 (and_3_out, P1_out, G0_out);
  and and_4 (and_4_out, P1_out, P0_out, P2_out, C0);
  and and_5 (and_5_out, P1_out, P2_out, G0_out);
  and and_6 (and_6_out, P2_out, G1_out);
  and and_7 (and_7_out, P0_out, P1_out, P2_out, P3_out, C0);
  and and_8 (and_8_out, P1_out, P2_out, P3_out, G0_out);
  and and_9 (and_9_out, P2_out, P3_out, G1_out);
  and and_10 (and_10_out, P3_out, G2_out);
  or or_1 (C1, G0_out, and_1_out);
  or or_2 (C2, and_3_out, and_2_out, G1_out);
  or or_3 (C3, and_4_out, and_5_out, and_6_out, G2_out);
  or or_4 (C4, and_7_out, and_8_out, and_9_out, and_10_out, G3_out);

  // Notes on the sheet:
  //   2207099
endmodule

// 4
module _4_bit_Parallel_Adder (
  input  in_1,
  input  [3:0] A,
  input  [3:0] B,
  output [3:0] C,
  output C4
);

  wire n4_bit_clag_1_c1, n4_bit_clag_1_c2, n4_bit_clag_1_c3;

  _4_bit_CLAG u_4_bit_clag_1 (
    .C0(in_1), .A(A), .B(B), .C1(n4_bit_clag_1_c1), .C2(n4_bit_clag_1_c2), .C3(n4_bit_clag_1_c3), .C4(C4));
  _1_bit_FA u_1_bit_fa_1 (.A(A[3]), .B(B[3]), .C_IN(n4_bit_clag_1_c3), .SUM(C[3]));  // open: C_OUT
  _1_bit_FA u_1_bit_fa_2 (.A(A[2]), .B(B[2]), .C_IN(n4_bit_clag_1_c2), .SUM(C[2]));  // open: C_OUT
  _1_bit_FA u_1_bit_fa_3 (.A(A[1]), .B(B[1]), .C_IN(n4_bit_clag_1_c1), .SUM(C[1]));  // open: C_OUT
  _1_bit_FA u_1_bit_fa_4 (.A(A[0]), .B(B[0]), .C_IN(in_1), .SUM(C[0]));  // open: C_OUT

  // Notes on the sheet:
  //   2207099
endmodule

// Adder
module _22_bit_Parallel_Adder (
  input  in_1,
  input  [21:0] in_2,
  input  [21:0] in_3,
  output zero,
  output Carry,
  output [21:0] Output,
  output Overflow
);

  wire n2_bit_parallel_adder_1_overflow, n4_bit_parallel_adder_1_c4, n4_bit_parallel_adder_2_c4,
       n4_bit_parallel_adder_3_c4, n4_bit_parallel_adder_4_c4, n4_bit_parallel_adder_5_c4;
  wire [21:0] bit_extender_1_out, xor_1_out;

  assign bit_extender_1_out = {{21{in_1}}, in_1};  // Bit_Extender bit_extender_1
  assign xor_1_out = in_3 ^ bit_extender_1_out;  // XOR_Gate xor_1, 22 bits wide
  _4_bit_Parallel_Adder u_4_bit_parallel_adder_1 (
    .in_1(in_1), .A(in_2[3:0]), .B(xor_1_out[3:0]), .C4(n4_bit_parallel_adder_1_c4), .C(Output[3:0]));
  _4_bit_Parallel_Adder u_4_bit_parallel_adder_2 (
    .in_1(n4_bit_parallel_adder_1_c4), .A(in_2[7:4]), .B(xor_1_out[7:4]), .C4(n4_bit_parallel_adder_2_c4),
    .C(Output[7:4]));
  _4_bit_Parallel_Adder u_4_bit_parallel_adder_3 (
    .in_1(n4_bit_parallel_adder_2_c4), .A(in_2[11:8]), .B(xor_1_out[11:8]), .C4(n4_bit_parallel_adder_3_c4),
    .C(Output[11:8]));
  _4_bit_Parallel_Adder u_4_bit_parallel_adder_4 (
    .in_1(n4_bit_parallel_adder_3_c4), .A(in_2[15:12]), .B(xor_1_out[15:12]),
    .C4(n4_bit_parallel_adder_4_c4), .C(Output[15:12]));
  _4_bit_Parallel_Adder u_4_bit_parallel_adder_5 (
    .in_1(n4_bit_parallel_adder_4_c4), .A(in_2[19:16]), .B(xor_1_out[19:16]),
    .C4(n4_bit_parallel_adder_5_c4), .C(Output[19:16]));
  _2_bit_Parallel_Adder u_2_bit_parallel_adder_1 (
    .in_1(n4_bit_parallel_adder_5_c4), .in_2(in_2[21:20]), .in_3(xor_1_out[21:20]), .C23(Carry),
    .C(Output[21:20]), .Overflow(n2_bit_parallel_adder_1_overflow));
  xor xor_2 (Overflow, n4_bit_parallel_adder_5_c4, n2_bit_parallel_adder_1_overflow);
  Zero zero_1 (.in_1(Output), .Zero(zero));

  // Notes on the sheet:
  //   2207099
endmodule

// 2
module _2_bit_Parallel_Adder (
  input  in_1,
  input  [1:0] in_2,
  input  [1:0] in_3,
  output [1:0] C,
  output C23,
  output Overflow
);

  wire n2_bit_clag_1_c1;

  _2_bit_CLAG u_2_bit_clag_1 (.in_1(in_1), .in_2(in_2), .in_3(in_3), .C1(n2_bit_clag_1_c1), .C2(C23));
  _1_bit_FA u_1_bit_fa_1 (.A(in_2[1]), .B(in_3[1]), .C_IN(n2_bit_clag_1_c1), .SUM(C[1]));  // open: C_OUT
  xor xor_1 (Overflow, C23, n2_bit_clag_1_c1);
  _1_bit_FA u_1_bit_fa_2 (.A(in_2[0]), .B(in_3[0]), .C_IN(in_1), .SUM(C[0]));  // open: C_OUT

  // Notes on the sheet:
  //   2207099
endmodule

// NEG
module Negative (
  input  [21:0] in_1,
  output C
);


  assign C = in_1[21];

  // Notes on the sheet:
  //   2207099
endmodule

// ZERO
module Zero (
  input  [21:0] in_1,
  output Zero
);

  wire or_1_out;

  or or_1 (or_1_out, in_1[0], in_1[1], in_1[2], in_1[3], in_1[4], in_1[5], in_1[6], in_1[7], in_1[8], in_1[9], in_1[10], in_1[11], in_1[12], in_1[13], in_1[14], in_1[15], in_1[16], in_1[17], in_1[18], in_1[19], in_1[20], in_1[21]);
  not not_1 (Zero, or_1_out);

  // Notes on the sheet:
  //   2207099
endmodule

module Booth (
  input  [21:0] M_input,
  input  [21:0] Q_input,
  input  Reset,
  output [21:0] Q,
  output [21:0] A
);

  wire A_out, CLK_out, or_1_out, Q_1_out, Q_1_q0, Q_out, sequence_decoder_1_c1,
       sequence_decoder_1_cl__a__q_1, sequence_decoder_1_dec_cnt, sequence_decoder_1_load__m__q__cnt,
       sequence_decoder_1_load_a, sequence_decoder_1_shr;
  wire [1:0] sequence_decoder_1_c0;
  wire [4:0] counter_1_q;
  wire [21:0] M_q21, main_1_output, n2_s_complement_1__2_s_comp, n2_s_complement_2__2_s_comp;

  Clock CLK (.out(CLK_out));
  Sequence_Decoder sequence_decoder_1 (
    .Clk(CLK_out), .Reset(Reset), .Q0(Q[0]), .Q_1(Q_1_q0), .Count(counter_1_q),
    .Cl__A__Q_1(sequence_decoder_1_cl__a__q_1), .LOad__M__Q__Cnt(sequence_decoder_1_load__m__q__cnt),
    .Load_A(sequence_decoder_1_load_a), .C0(sequence_decoder_1_c0[0]), .C1(sequence_decoder_1_c1),
    .Shr(sequence_decoder_1_shr), .Dec_Cnt(sequence_decoder_1_dec_cnt));
  or or_1 (or_1_out, sequence_decoder_1_load__m__q__cnt, sequence_decoder_1_dec_cnt);
  Counter #(.width(5), .max('h1f)) counter_1 (
    .load(or_1_out), .D(5'b10110), .count(sequence_decoder_1_dec_cnt), .Q(counter_1_q), .clk(CLK_out));  // open: carry, clr
  // Probe on M_input
  // Probe on n2_s_complement_1__2_s_comp
  _2_s_Complement u_2_s_complement_1 (.\input (Q_input), ._2_s_Comp(n2_s_complement_1__2_s_comp));
  not not_1 (sequence_decoder_1_c0[1], sequence_decoder_1_c1);
  _2_s_Complement u_2_s_complement_2 (.\input (M_input), ._2_s_Comp(n2_s_complement_2__2_s_comp));
  Shift_Register #(.length(22)) u_A (
    .shift(sequence_decoder_1_shr), .in(A[21]), .clk(CLK_out), .out(A_out), .load(sequence_decoder_1_load_a),
    .clr(sequence_decoder_1_cl__a__q_1), .d0(main_1_output[21]), .q0(A[21]), .d1(main_1_output[20]),
    .q1(A[20]), .d2(main_1_output[19]), .q2(A[19]), .d3(main_1_output[18]), .q3(A[18]),
    .d4(main_1_output[17]), .q4(A[17]), .d5(main_1_output[16]), .q5(A[16]), .d6(main_1_output[15]),
    .q6(A[15]), .d7(main_1_output[14]), .q7(A[14]), .d8(main_1_output[13]), .q8(A[13]),
    .d9(main_1_output[12]), .q9(A[12]), .d10(main_1_output[11]), .q10(A[11]), .d11(main_1_output[10]),
    .q11(A[10]), .d12(main_1_output[9]), .q12(A[9]), .d13(main_1_output[8]), .q13(A[8]),
    .d14(main_1_output[7]), .q14(A[7]), .d15(main_1_output[6]), .q15(A[6]), .d16(main_1_output[5]),
    .q16(A[5]), .d17(main_1_output[4]), .q17(A[4]), .d18(main_1_output[3]), .q18(A[3]),
    .d19(main_1_output[2]), .q19(A[2]), .d20(main_1_output[1]), .q20(A[1]), .d21(main_1_output[0]), .q21(A[0]));
  Shift_Register #(.length(22)) M (
    .shift(1'b0), .clk(CLK_out), .load(sequence_decoder_1_load__m__q__cnt),
    .d0(n2_s_complement_2__2_s_comp[21]), .q0(M_q21[21]), .d1(n2_s_complement_2__2_s_comp[20]),
    .q1(M_q21[20]), .d2(n2_s_complement_2__2_s_comp[19]), .q2(M_q21[19]),
    .d3(n2_s_complement_2__2_s_comp[18]), .q3(M_q21[18]), .d4(n2_s_complement_2__2_s_comp[17]),
    .q4(M_q21[17]), .d5(n2_s_complement_2__2_s_comp[16]), .q5(M_q21[16]),
    .d6(n2_s_complement_2__2_s_comp[15]), .q6(M_q21[15]), .d7(n2_s_complement_2__2_s_comp[14]),
    .q7(M_q21[14]), .d8(n2_s_complement_2__2_s_comp[13]), .q8(M_q21[13]),
    .d9(n2_s_complement_2__2_s_comp[12]), .q9(M_q21[12]), .d10(n2_s_complement_2__2_s_comp[11]),
    .q10(M_q21[11]), .d11(n2_s_complement_2__2_s_comp[10]), .q11(M_q21[10]),
    .d12(n2_s_complement_2__2_s_comp[9]), .q12(M_q21[9]), .d13(n2_s_complement_2__2_s_comp[8]),
    .q13(M_q21[8]), .d14(n2_s_complement_2__2_s_comp[7]), .q14(M_q21[7]),
    .d15(n2_s_complement_2__2_s_comp[6]), .q15(M_q21[6]), .d16(n2_s_complement_2__2_s_comp[5]),
    .q16(M_q21[5]), .d17(n2_s_complement_2__2_s_comp[4]), .q17(M_q21[4]),
    .d18(n2_s_complement_2__2_s_comp[3]), .q18(M_q21[3]), .d19(n2_s_complement_2__2_s_comp[2]),
    .q19(M_q21[2]), .d20(n2_s_complement_2__2_s_comp[1]), .q20(M_q21[1]),
    .d21(n2_s_complement_2__2_s_comp[0]), .q21(M_q21[0]));  // open: in, out, clr
  main main_1 (
    .Control(sequence_decoder_1_c0), .A(A), .B(M_q21), .Output(main_1_output));  // open: Negative, Zero, Overflow, Carry
  // Probe on A
  Shift_Register #(.length(22)) u_Q (
    .shift(sequence_decoder_1_shr), .in(A_out), .clk(CLK_out), .out(Q_out),
    .load(sequence_decoder_1_load__m__q__cnt), .d0(n2_s_complement_1__2_s_comp[21]), .q0(Q[21]),
    .d1(n2_s_complement_1__2_s_comp[20]), .q1(Q[20]), .d2(n2_s_complement_1__2_s_comp[19]), .q2(Q[19]),
    .d3(n2_s_complement_1__2_s_comp[18]), .q3(Q[18]), .d4(n2_s_complement_1__2_s_comp[17]), .q4(Q[17]),
    .d5(n2_s_complement_1__2_s_comp[16]), .q5(Q[16]), .d6(n2_s_complement_1__2_s_comp[15]), .q6(Q[15]),
    .d7(n2_s_complement_1__2_s_comp[14]), .q7(Q[14]), .d8(n2_s_complement_1__2_s_comp[13]), .q8(Q[13]),
    .d9(n2_s_complement_1__2_s_comp[12]), .q9(Q[12]), .d10(n2_s_complement_1__2_s_comp[11]), .q10(Q[11]),
    .d11(n2_s_complement_1__2_s_comp[10]), .q11(Q[10]), .d12(n2_s_complement_1__2_s_comp[9]), .q12(Q[9]),
    .d13(n2_s_complement_1__2_s_comp[8]), .q13(Q[8]), .d14(n2_s_complement_1__2_s_comp[7]), .q14(Q[7]),
    .d15(n2_s_complement_1__2_s_comp[6]), .q15(Q[6]), .d16(n2_s_complement_1__2_s_comp[5]), .q16(Q[5]),
    .d17(n2_s_complement_1__2_s_comp[4]), .q17(Q[4]), .d18(n2_s_complement_1__2_s_comp[3]), .q18(Q[3]),
    .d19(n2_s_complement_1__2_s_comp[2]), .q19(Q[2]), .d20(n2_s_complement_1__2_s_comp[1]), .q20(Q[1]),
    .d21(n2_s_complement_1__2_s_comp[0]), .q21(Q[0]));  // open: clr
  Shift_Register #(.length(1)) Q_1 (
    .shift(sequence_decoder_1_shr), .in(Q_out), .clk(CLK_out), .out(Q_1_out),
    .clr(sequence_decoder_1_cl__a__q_1), .q0(Q_1_q0));  // open: load, d0
  // Probe on Q

  // Notes on the sheet:
  //   2207099
endmodule

module state_traverse (
  input  [1:0] Q,
  input  [2:0] T,
  input  C,
  output DA,
  output DB,
  output DC
);

  wire and_1_out, and_2_out, and_3_out, and_4_out, and_5_out, or_4_out, or_5_out, Q0, Q1, Q2, Q3, T0, T1, T2,
       T3, T4, T5, T6, T7;

  Decoder #(.select(2), .enable("false")) decoder_1 (.out0(Q0), .out1(Q1), .out2(Q2), .out3(Q3), .sel(Q));
  Decoder #(.select(3), .enable("false")) decoder_2 (
    .out0(T0), .out1(T1), .out2(T2), .out3(T3), .out4(T4), .out5(T5), .out6(T6), .out7(T7), .sel(T));
  or or_1 (DA, T0, and_5_out, T3, T4, and_1_out, T7);
  or or_2 (DB, T1, and_2_out, T5, T6, T6, T7);
  or or_3 (DC, T5, and_3_out, T3, T4, and_4_out, T7);
  and and_1 (and_1_out, T6, C);
  and and_2 (and_2_out, T2, Q2);
  and and_3 (and_3_out, T2, or_5_out);
  and and_4 (and_4_out, T6, C);
  and and_5 (and_5_out, T2, or_4_out);
  or or_4 (or_4_out, Q0, Q2, Q3);
  or or_5 (or_5_out, Q0, Q1, Q3);

  // Notes on the sheet:
  //   2207099
endmodule

module Sequence_Decoder (
  input  Clk,
  input  Reset,
  input  Q0,
  input  Q_1,
  input  [4:0] Count,
  output Cl__A__Q_1,
  output LOad__M__Q__Cnt,
  output Load_A,
  output C0,
  output C1,
  output Shr,
  output Dec_Cnt
);

  wire nor_1_out, state_traverse_1_da, state_traverse_1_db, state_traverse_1_dc, T0, T2, T4, T6, T7;
  wire [2:0] T;

  nor nor_1 (nor_1_out, Count[0], Count[1], Count[2], Count[3], Count[4]);
  Decoder #(.select(3), .enable("false")) decoder_1 (
    .out0(T0), .out1(Cl__A__Q_1), .out2(T2), .out3(C0), .out4(T4), .out5(Dec_Cnt), .out6(T6), .out7(T7),
    .sel(T));
  state_traverse state_traverse_1 (
    .Q({Q0, Q_1}), .T(T), .C(nor_1_out), .DA(state_traverse_1_da), .DB(state_traverse_1_db),
    .DC(state_traverse_1_dc));
  D_Flip_Flop d_ff_1 (.clk(Clk), .D(state_traverse_1_da), .Q(T[0]), .reset(Reset));  // open: Qn, preset, en
  D_Flip_Flop d_ff_2 (.clk(Clk), .D(state_traverse_1_db), .Q(T[1]), .reset(Reset));  // open: Qn, preset, en
  D_Flip_Flop d_ff_3 (.clk(Clk), .D(state_traverse_1_dc), .Q(T[2]), .reset(Reset));  // open: Qn, preset, en
  or or_1 (Load_A, C0, T4);
  or or_2 (C1, T4, C0);

  assign LOad__M__Q__Cnt = Cl__A__Q_1;
  assign Shr = Dec_Cnt;

  // Other names for the same wires on the sheet: T1 = Cl__A__Q_1; T3 = C0; T5 = Dec_Cnt

  // Notes on the sheet:
  //   2207099
endmodule

module _2_s_Complement (
  input  [21:0] \input ,
  output [21:0] _2_s_Comp
);

  wire [20:0] not_1_out;
  wire [21:0] adder_1_out;

  not not_1 (not_1_out[0], \input [0]);
  not not_2 (not_1_out[1], \input [1]);
  not not_3 (not_1_out[2], \input [2]);
  not not_4 (not_1_out[3], \input [3]);
  not not_5 (not_1_out[4], \input [4]);
  not not_6 (not_1_out[5], \input [5]);
  not not_7 (not_1_out[6], \input [6]);
  not not_8 (not_1_out[7], \input [7]);
  not not_9 (not_1_out[8], \input [8]);
  not not_10 (not_1_out[9], \input [9]);
  not not_11 (not_1_out[10], \input [10]);
  not not_12 (not_1_out[11], \input [11]);
  not not_13 (not_1_out[12], \input [12]);
  not not_14 (not_1_out[13], \input [13]);
  not not_15 (not_1_out[14], \input [14]);
  not not_16 (not_1_out[15], \input [15]);
  not not_17 (not_1_out[16], \input [16]);
  not not_18 (not_1_out[17], \input [17]);
  not not_19 (not_1_out[18], \input [18]);
  not not_20 (not_1_out[19], \input [19]);
  not not_21 (not_1_out[20], \input [20]);
  Adder #(.width(22)) adder_1 (.a({\input [21], not_1_out}), .b(22'h1), .out(adder_1_out));  // open: cin, cout
  Multiplexer #(.width(22), .enable("false")) multiplexer_1 (
    .in0(\input ), .in1(adder_1_out), .out(_2_s_Comp), .sel(\input [21]));

  // Notes on the sheet:
  //   2207099
endmodule

module Parallel_Load_Register (
  input  Load,
  input  [21:0] In,
  input  CLR,
  output [21:0] Out
);

  wire and_1_out, and_2_out, and_3_out, and_4_out, and_5_out, and_6_out, and_7_out, and_8_out, and_9_out,
       and_10_out, and_11_out, and_12_out, and_13_out, and_14_out, and_15_out, and_16_out, and_17_out,
       and_18_out, and_19_out, and_20_out, and_21_out, and_22_out, and_23_out, and_24_out, and_25_out,
       and_26_out, and_27_out, and_28_out, and_29_out, and_30_out, and_31_out, and_32_out, and_33_out,
       and_34_out, and_35_out, and_36_out, and_37_out, and_38_out, and_39_out, and_40_out, and_41_out,
       and_42_out, and_43_out, and_44_out, CP_out, not_1_out, not_2_out, not_3_out, not_4_out, not_5_out,
       not_6_out, not_7_out, not_8_out, not_9_out, not_10_out, not_11_out, not_12_out, not_13_out,
       not_14_out, not_15_out, not_16_out, not_17_out, not_18_out, not_19_out, not_20_out, not_21_out,
       not_22_out;

  Clock CP (.out(CP_out));
  not not_1 (not_1_out, In[0]);
  not not_2 (not_2_out, In[1]);
  not not_3 (not_3_out, In[2]);
  not not_4 (not_4_out, In[3]);
  not not_5 (not_5_out, In[4]);
  not not_6 (not_6_out, In[5]);
  not not_7 (not_7_out, In[6]);
  not not_8 (not_8_out, In[7]);
  not not_9 (not_9_out, In[8]);
  not not_10 (not_10_out, In[9]);
  not not_11 (not_11_out, In[10]);
  not not_12 (not_12_out, In[11]);
  not not_13 (not_13_out, In[12]);
  not not_14 (not_14_out, In[13]);
  not not_15 (not_15_out, In[14]);
  not not_16 (not_16_out, In[15]);
  not not_17 (not_17_out, In[16]);
  not not_18 (not_18_out, In[17]);
  not not_19 (not_19_out, In[18]);
  not not_20 (not_20_out, In[19]);
  not not_21 (not_21_out, In[20]);
  not not_22 (not_22_out, In[21]);
  and and_1 (and_1_out, In[0], Load);
  and and_2 (and_2_out, not_1_out, Load);
  and and_3 (and_3_out, In[1], Load);
  and and_4 (and_4_out, not_2_out, Load);
  and and_5 (and_5_out, In[2], Load);
  and and_6 (and_6_out, not_3_out, Load);
  and and_7 (and_7_out, In[3], Load);
  and and_8 (and_8_out, not_4_out, Load);
  and and_9 (and_9_out, In[4], Load);
  and and_10 (and_10_out, not_5_out, Load);
  and and_11 (and_11_out, In[5], Load);
  and and_12 (and_12_out, not_6_out, Load);
  and and_13 (and_13_out, In[6], Load);
  and and_14 (and_14_out, not_7_out, Load);
  and and_15 (and_15_out, In[7], Load);
  and and_16 (and_16_out, not_8_out, Load);
  and and_17 (and_17_out, In[8], Load);
  and and_18 (and_18_out, not_9_out, Load);
  and and_19 (and_19_out, In[9], Load);
  and and_20 (and_20_out, not_10_out, Load);
  and and_21 (and_21_out, In[10], Load);
  and and_22 (and_22_out, not_11_out, Load);
  and and_23 (and_23_out, In[11], Load);
  and and_24 (and_24_out, not_12_out, Load);
  and and_25 (and_25_out, In[12], Load);
  and and_26 (and_26_out, not_13_out, Load);
  and and_27 (and_27_out, In[13], Load);
  and and_28 (and_28_out, not_14_out, Load);
  and and_29 (and_29_out, In[14], Load);
  and and_30 (and_30_out, not_15_out, Load);
  and and_31 (and_31_out, In[15], Load);
  and and_32 (and_32_out, not_16_out, Load);
  and and_33 (and_33_out, In[16], Load);
  and and_34 (and_34_out, not_17_out, Load);
  and and_35 (and_35_out, In[17], Load);
  and and_36 (and_36_out, not_18_out, Load);
  and and_37 (and_37_out, In[18], Load);
  and and_38 (and_38_out, not_19_out, Load);
  and and_39 (and_39_out, In[19], Load);
  and and_40 (and_40_out, not_20_out, Load);
  and and_41 (and_41_out, In[20], Load);
  and and_42 (and_42_out, not_21_out, Load);
  and and_43 (and_43_out, In[21], Load);
  and and_44 (and_44_out, not_22_out, Load);
  J_K_Flip_Flop j_k_ff_1 (.J(and_1_out), .clk(CP_out), .K(and_2_out), .Q(Out[0]), .reset(CLR));  // open: Qn, preset, en
  J_K_Flip_Flop j_k_ff_2 (.J(and_3_out), .clk(CP_out), .K(and_4_out), .Q(Out[1]), .reset(CLR));  // open: Qn, preset, en
  J_K_Flip_Flop j_k_ff_3 (.J(and_5_out), .clk(CP_out), .K(and_6_out), .Q(Out[2]), .reset(CLR));  // open: Qn, preset, en
  J_K_Flip_Flop j_k_ff_4 (.J(and_7_out), .clk(CP_out), .K(and_8_out), .Q(Out[3]), .reset(CLR));  // open: Qn, preset, en
  J_K_Flip_Flop j_k_ff_5 (
    .J(and_9_out), .clk(CP_out), .K(and_10_out), .Q(Out[4]), .reset(CLR));  // open: Qn, preset, en
  J_K_Flip_Flop j_k_ff_6 (
    .J(and_11_out), .clk(CP_out), .K(and_12_out), .Q(Out[5]), .reset(CLR));  // open: Qn, preset, en
  J_K_Flip_Flop j_k_ff_7 (
    .J(and_13_out), .clk(CP_out), .K(and_14_out), .Q(Out[6]), .reset(CLR));  // open: Qn, preset, en
  J_K_Flip_Flop j_k_ff_8 (
    .J(and_15_out), .clk(CP_out), .K(and_16_out), .Q(Out[7]), .reset(CLR));  // open: Qn, preset, en
  J_K_Flip_Flop j_k_ff_9 (
    .J(and_17_out), .clk(CP_out), .K(and_18_out), .Q(Out[8]), .reset(CLR));  // open: Qn, preset, en
  J_K_Flip_Flop j_k_ff_10 (
    .J(and_19_out), .clk(CP_out), .K(and_20_out), .Q(Out[9]), .reset(CLR));  // open: Qn, preset, en
  J_K_Flip_Flop j_k_ff_11 (
    .J(and_21_out), .clk(CP_out), .K(and_22_out), .Q(Out[10]), .reset(CLR));  // open: Qn, preset, en
  J_K_Flip_Flop j_k_ff_12 (
    .J(and_23_out), .clk(CP_out), .K(and_24_out), .Q(Out[11]), .reset(CLR));  // open: Qn, preset, en
  J_K_Flip_Flop j_k_ff_13 (
    .J(and_25_out), .clk(CP_out), .K(and_26_out), .Q(Out[12]), .reset(CLR));  // open: Qn, preset, en
  J_K_Flip_Flop j_k_ff_14 (
    .J(and_27_out), .clk(CP_out), .K(and_28_out), .Q(Out[13]), .reset(CLR));  // open: Qn, preset, en
  J_K_Flip_Flop j_k_ff_15 (
    .J(and_29_out), .clk(CP_out), .K(and_30_out), .Q(Out[14]), .reset(CLR));  // open: Qn, preset, en
  J_K_Flip_Flop j_k_ff_16 (
    .J(and_31_out), .clk(CP_out), .K(and_32_out), .Q(Out[15]), .reset(CLR));  // open: Qn, preset, en
  J_K_Flip_Flop j_k_ff_17 (
    .J(and_33_out), .clk(CP_out), .K(and_34_out), .Q(Out[16]), .reset(CLR));  // open: Qn, preset, en
  J_K_Flip_Flop j_k_ff_18 (
    .J(and_35_out), .clk(CP_out), .K(and_36_out), .Q(Out[17]), .reset(CLR));  // open: Qn, preset, en
  J_K_Flip_Flop j_k_ff_19 (
    .J(and_37_out), .clk(CP_out), .K(and_38_out), .Q(Out[18]), .reset(CLR));  // open: Qn, preset, en
  J_K_Flip_Flop j_k_ff_20 (
    .J(and_39_out), .clk(CP_out), .K(and_40_out), .Q(Out[19]), .reset(CLR));  // open: Qn, preset, en
  J_K_Flip_Flop j_k_ff_21 (
    .J(and_41_out), .clk(CP_out), .K(and_42_out), .Q(Out[20]), .reset(CLR));  // open: Qn, preset, en
  J_K_Flip_Flop j_k_ff_22 (
    .J(and_43_out), .clk(CP_out), .K(and_44_out), .Q(Out[21]), .reset(CLR));  // open: Qn, preset, en

  // Notes on the sheet:
  //   2207099
endmodule

module Counter_Load_Register (
  input  Counter,
  input  Load,
  input  I1,
  input  I2,
  input  I3,
  input  I4,
  input  CLR,
  output A1,
  output A2,
  output A3,
  output A4,
  output Carry_Out
);

  wire and_1_out, and_2_out, and_3_out, and_4_out, and_5_out, and_6_out, and_7_out, and_8_out, and_9_out,
       and_10_out, and_11_out, and_12_out, CLK_out, not_1_out, not_2_out, not_3_out, not_4_out, not_5_out,
       not_6_out, or_1_out, or_2_out, or_3_out, or_4_out, or_5_out, or_6_out, or_7_out, or_8_out;

  not not_1 (not_1_out, Load);
  Clock CLK (.out(CLK_out));
  and and_1 (and_1_out, Counter, not_1_out);
  not not_2 (not_2_out, not_1_out);
  not not_3 (not_3_out, I1);
  not not_4 (not_4_out, I2);
  not not_5 (not_5_out, I3);
  not not_6 (not_6_out, I4);
  and and_2 (and_2_out, I1, not_2_out);
  and and_3 (and_3_out, not_2_out, not_3_out);
  and and_4 (and_4_out, I2, not_2_out);
  and and_5 (and_5_out, not_2_out, not_4_out);
  and and_6 (and_6_out, I3, not_2_out);
  and and_7 (and_7_out, not_2_out, not_5_out);
  and and_8 (and_8_out, I4, not_2_out);
  and and_9 (and_9_out, not_2_out, not_6_out);
  and and_10 (and_10_out, and_1_out, A1);
  and and_11 (and_11_out, and_1_out, A1, A2);
  and and_12 (and_12_out, and_1_out, A1, A2, A3);
  and and_13 (Carry_Out, and_1_out, A1, A2, A3, A4);
  or or_1 (or_1_out, and_2_out, and_1_out);
  or or_2 (or_2_out, and_1_out, and_3_out);
  or or_3 (or_3_out, and_4_out, and_10_out);
  or or_4 (or_4_out, and_10_out, and_5_out);
  or or_5 (or_5_out, and_6_out, and_11_out);
  or or_6 (or_6_out, and_11_out, and_7_out);
  or or_7 (or_7_out, and_8_out, and_12_out);
  or or_8 (or_8_out, and_12_out, and_9_out);
  J_K_Flip_Flop j_k_ff_1 (.J(or_1_out), .clk(CLK_out), .K(or_2_out), .Q(A1), .reset(CLR));  // open: Qn, preset, en
  J_K_Flip_Flop j_k_ff_2 (.J(or_3_out), .clk(CLK_out), .K(or_4_out), .Q(A2), .reset(CLR));  // open: Qn, preset, en
  J_K_Flip_Flop j_k_ff_3 (.J(or_5_out), .clk(CLK_out), .K(or_6_out), .Q(A3), .reset(CLR));  // open: Qn, preset, en
  J_K_Flip_Flop j_k_ff_4 (.J(or_7_out), .clk(CLK_out), .K(or_8_out), .Q(A4), .reset(CLR));  // open: Qn, preset, en

  // Notes on the sheet:
  //   2207099
endmodule

// CL 4
module Counter___Load_4_bit (
  input  Cin,
  input  Counter,
  input  Load,
  input  I1,
  input  I2,
  input  I3,
  input  I4,
  input  CLK,
  input  CLR,
  output A1,
  output A2,
  output A3,
  output A4,
  output Carry_Out
);

  wire and_1_out, and_2_out, and_3_out, and_4_out, and_5_out, and_6_out, and_7_out, and_8_out, and_9_out,
       and_10_out, and_11_out, and_12_out, and_13_out, not_1_out, not_2_out, not_3_out, not_4_out, not_5_out,
       not_6_out, or_1_out, or_2_out, or_3_out, or_4_out, or_5_out, or_6_out, or_7_out, or_8_out;

  not not_1 (not_1_out, Load);
  and and_1 (and_1_out, Counter, not_1_out);
  not not_2 (not_2_out, not_1_out);
  not not_3 (not_3_out, I1);
  not not_4 (not_4_out, I2);
  not not_5 (not_5_out, I3);
  not not_6 (not_6_out, I4);
  and and_2 (and_2_out, I1, not_2_out);
  and and_3 (and_3_out, not_2_out, not_3_out);
  and and_4 (and_4_out, I2, not_2_out);
  and and_5 (and_5_out, not_2_out, not_4_out);
  and and_6 (and_6_out, I3, not_2_out);
  and and_7 (and_7_out, not_2_out, not_5_out);
  and and_8 (and_8_out, I4, not_2_out);
  and and_9 (and_9_out, not_2_out, not_6_out);
  and and_10 (and_10_out, and_1_out, Cin);
  and and_11 (and_11_out, and_1_out, Cin, A1);
  and and_12 (and_12_out, and_1_out, A1, A2, Cin);
  and and_13 (and_13_out, and_1_out, A1, Cin, A2, A3);
  and and_14 (Carry_Out, Cin, and_1_out, A1, A2, A3, A4);
  or or_1 (or_1_out, and_2_out, and_10_out);
  or or_2 (or_2_out, and_10_out, and_3_out);
  or or_3 (or_3_out, and_4_out, and_11_out);
  or or_4 (or_4_out, and_11_out, and_5_out);
  or or_5 (or_5_out, and_6_out, and_12_out);
  or or_6 (or_6_out, and_12_out, and_7_out);
  or or_7 (or_7_out, and_8_out, and_13_out);
  or or_8 (or_8_out, and_13_out, and_9_out);
  J_K_Flip_Flop j_k_ff_1 (.J(or_1_out), .clk(CLK), .K(or_2_out), .Q(A1), .reset(CLR));  // open: Qn, preset, en
  J_K_Flip_Flop j_k_ff_2 (.J(or_3_out), .clk(CLK), .K(or_4_out), .Q(A2), .reset(CLR));  // open: Qn, preset, en
  J_K_Flip_Flop j_k_ff_3 (.J(or_5_out), .clk(CLK), .K(or_6_out), .Q(A3), .reset(CLR));  // open: Qn, preset, en
  J_K_Flip_Flop j_k_ff_4 (.J(or_7_out), .clk(CLK), .K(or_8_out), .Q(A4), .reset(CLR));  // open: Qn, preset, en

  // Notes on the sheet:
  //   2207099
endmodule

// CL 2
module CL_2_bit (
  input  Cin,
  input  Counter,
  input  Load,
  input  I1,
  input  I2,
  input  CLK,
  input  CLR,
  output A1,
  output A2,
  output Carry_Out
);

  wire and_1_out, and_2_out, and_3_out, and_4_out, and_5_out, and_6_out, and_7_out, not_1_out, not_2_out,
       not_3_out, not_4_out, or_1_out, or_2_out, or_3_out, or_4_out;

  not not_1 (not_1_out, Load);
  and and_1 (and_1_out, Counter, not_1_out);
  not not_2 (not_2_out, not_1_out);
  not not_3 (not_3_out, I1);
  not not_4 (not_4_out, I2);
  and and_2 (and_2_out, I1, not_2_out);
  and and_3 (and_3_out, not_2_out, not_3_out);
  and and_4 (and_4_out, I2, not_2_out);
  and and_5 (and_5_out, not_2_out, not_4_out);
  and and_6 (and_6_out, and_1_out, Cin);
  and and_7 (and_7_out, and_1_out, Cin, A1);
  and and_8 (Carry_Out, Cin, and_1_out, A1, A2);
  or or_1 (or_1_out, and_2_out, and_6_out);
  or or_2 (or_2_out, and_6_out, and_3_out);
  or or_3 (or_3_out, and_4_out, and_7_out);
  or or_4 (or_4_out, and_7_out, and_5_out);
  J_K_Flip_Flop j_k_ff_1 (.J(or_1_out), .clk(CLK), .K(or_2_out), .Q(A1), .reset(CLR));  // open: Qn, preset, en
  J_K_Flip_Flop j_k_ff_2 (.J(or_3_out), .clk(CLK), .K(or_4_out), .Q(A2), .reset(CLR));  // open: Qn, preset, en

  // Notes on the sheet:
  //   2207099
endmodule

module CL_22_bit (
  input  Counter,
  input  Load,
  input  [21:0] IN,
  input  CLR,
  output [21:0] OUT
);

  wire CLK, counter_load_4_bit_1_carry_out, counter_load_4_bit_2_carry_out, counter_load_4_bit_3_carry_out,
       counter_load_4_bit_4_carry_out, counter_load_4_bit_5_carry_out;

  Clock u_CLK (.out(CLK));
  Counter___Load_4_bit counter_load_4_bit_1 (
    .Cin(Counter), .Counter(Counter), .Load(Load), .I1(IN[0]), .I2(IN[1]), .I3(IN[2]), .I4(IN[3]),
    .A1(OUT[0]), .A2(OUT[1]), .A3(OUT[2]), .A4(OUT[3]), .Carry_Out(counter_load_4_bit_1_carry_out),
    .CLR(CLR), .CLK(CLK));
  Counter___Load_4_bit counter_load_4_bit_2 (
    .Cin(counter_load_4_bit_1_carry_out), .Counter(Counter), .Load(Load), .I1(IN[4]), .I2(IN[5]), .I3(IN[6]),
    .I4(IN[7]), .A1(OUT[4]), .A2(OUT[5]), .A3(OUT[6]), .A4(OUT[7]),
    .Carry_Out(counter_load_4_bit_2_carry_out), .CLR(CLR), .CLK(CLK));
  Counter___Load_4_bit counter_load_4_bit_3 (
    .Cin(counter_load_4_bit_2_carry_out), .Counter(Counter), .Load(Load), .I1(IN[8]), .I2(IN[9]),
    .I3(IN[10]), .I4(IN[11]), .A1(OUT[8]), .A2(OUT[9]), .A3(OUT[10]), .A4(OUT[11]),
    .Carry_Out(counter_load_4_bit_3_carry_out), .CLR(CLR), .CLK(CLK));
  Counter___Load_4_bit counter_load_4_bit_4 (
    .Cin(counter_load_4_bit_3_carry_out), .Counter(Counter), .Load(Load), .I1(IN[12]), .I2(IN[13]),
    .I3(IN[14]), .I4(IN[15]), .A1(OUT[12]), .A2(OUT[13]), .A3(OUT[14]), .A4(OUT[15]),
    .Carry_Out(counter_load_4_bit_4_carry_out), .CLR(CLR), .CLK(CLK));
  Counter___Load_4_bit counter_load_4_bit_5 (
    .Cin(counter_load_4_bit_4_carry_out), .Counter(Counter), .Load(Load), .I1(IN[16]), .I2(IN[17]),
    .I3(IN[18]), .I4(IN[19]), .A1(OUT[16]), .A2(OUT[17]), .A3(OUT[18]), .A4(OUT[19]),
    .Carry_Out(counter_load_4_bit_5_carry_out), .CLR(CLR), .CLK(CLK));
  CL_2_bit cl_2_bit_1 (
    .Cin(counter_load_4_bit_5_carry_out), .Counter(Counter), .Load(Load), .I1(IN[20]), .I2(IN[21]),
    .CLR(CLR), .A1(OUT[20]), .A2(OUT[21]), .CLK(CLK));  // open: Carry_Out
  // Probe on OUT

  // Other names for the same wires on the sheet: Count = Counter

  // Notes on the sheet:
  //   2207099
endmodule

// AC
module Accumulator (
  input  Load,
  input  [21:0] In,
  input  CLk,
  input  CLR,
  output [21:0] Out
);

  wire and_1_out, and_2_out, and_3_out, and_4_out, and_5_out, and_6_out, and_7_out, and_8_out, and_9_out,
       and_10_out, and_11_out, and_12_out, and_13_out, and_14_out, and_15_out, and_16_out, and_17_out,
       and_18_out, and_19_out, and_20_out, and_21_out, and_22_out, and_23_out, and_24_out, and_25_out,
       and_26_out, and_27_out, and_28_out, and_29_out, and_30_out, and_31_out, and_32_out, and_33_out,
       and_34_out, and_35_out, and_36_out, and_37_out, and_38_out, and_39_out, and_40_out, and_41_out,
       and_42_out, and_43_out, and_44_out, not_1_out, not_2_out, not_3_out, not_4_out, not_5_out, not_6_out,
       not_7_out, not_8_out, not_9_out, not_10_out, not_11_out, not_12_out, not_13_out, not_14_out,
       not_15_out, not_16_out, not_17_out, not_18_out, not_19_out, not_20_out, not_21_out, not_22_out;

  not not_1 (not_1_out, In[0]);
  not not_2 (not_2_out, In[1]);
  not not_3 (not_3_out, In[2]);
  not not_4 (not_4_out, In[3]);
  not not_5 (not_5_out, In[4]);
  not not_6 (not_6_out, In[5]);
  not not_7 (not_7_out, In[6]);
  not not_8 (not_8_out, In[7]);
  not not_9 (not_9_out, In[8]);
  not not_10 (not_10_out, In[9]);
  not not_11 (not_11_out, In[10]);
  not not_12 (not_12_out, In[11]);
  not not_13 (not_13_out, In[12]);
  not not_14 (not_14_out, In[13]);
  not not_15 (not_15_out, In[14]);
  not not_16 (not_16_out, In[15]);
  not not_17 (not_17_out, In[16]);
  not not_18 (not_18_out, In[17]);
  not not_19 (not_19_out, In[18]);
  not not_20 (not_20_out, In[19]);
  not not_21 (not_21_out, In[20]);
  not not_22 (not_22_out, In[21]);
  and and_1 (and_1_out, In[0], Load);
  and and_2 (and_2_out, not_1_out, Load);
  and and_3 (and_3_out, In[1], Load);
  and and_4 (and_4_out, not_2_out, Load);
  and and_5 (and_5_out, In[2], Load);
  and and_6 (and_6_out, not_3_out, Load);
  and and_7 (and_7_out, In[3], Load);
  and and_8 (and_8_out, not_4_out, Load);
  and and_9 (and_9_out, In[4], Load);
  and and_10 (and_10_out, not_5_out, Load);
  and and_11 (and_11_out, In[5], Load);
  and and_12 (and_12_out, not_6_out, Load);
  and and_13 (and_13_out, In[6], Load);
  and and_14 (and_14_out, not_7_out, Load);
  and and_15 (and_15_out, In[7], Load);
  and and_16 (and_16_out, not_8_out, Load);
  and and_17 (and_17_out, In[8], Load);
  and and_18 (and_18_out, not_9_out, Load);
  and and_19 (and_19_out, In[9], Load);
  and and_20 (and_20_out, not_10_out, Load);
  and and_21 (and_21_out, In[10], Load);
  and and_22 (and_22_out, not_11_out, Load);
  and and_23 (and_23_out, In[11], Load);
  and and_24 (and_24_out, not_12_out, Load);
  and and_25 (and_25_out, In[12], Load);
  and and_26 (and_26_out, not_13_out, Load);
  and and_27 (and_27_out, In[13], Load);
  and and_28 (and_28_out, not_14_out, Load);
  and and_29 (and_29_out, In[14], Load);
  and and_30 (and_30_out, not_15_out, Load);
  and and_31 (and_31_out, In[15], Load);
  and and_32 (and_32_out, not_16_out, Load);
  and and_33 (and_33_out, In[16], Load);
  and and_34 (and_34_out, not_17_out, Load);
  and and_35 (and_35_out, In[17], Load);
  and and_36 (and_36_out, not_18_out, Load);
  and and_37 (and_37_out, In[18], Load);
  and and_38 (and_38_out, not_19_out, Load);
  and and_39 (and_39_out, In[19], Load);
  and and_40 (and_40_out, not_20_out, Load);
  and and_41 (and_41_out, In[20], Load);
  and and_42 (and_42_out, not_21_out, Load);
  and and_43 (and_43_out, In[21], Load);
  and and_44 (and_44_out, not_22_out, Load);
  J_K_Flip_Flop j_k_ff_1 (.J(and_1_out), .clk(CLk), .K(and_2_out), .Q(Out[0]), .reset(CLR));  // open: Qn, preset, en
  J_K_Flip_Flop j_k_ff_2 (.J(and_3_out), .clk(CLk), .K(and_4_out), .Q(Out[1]), .reset(CLR));  // open: Qn, preset, en
  J_K_Flip_Flop j_k_ff_3 (.J(and_5_out), .clk(CLk), .K(and_6_out), .Q(Out[2]), .reset(CLR));  // open: Qn, preset, en
  J_K_Flip_Flop j_k_ff_4 (.J(and_7_out), .clk(CLk), .K(and_8_out), .Q(Out[3]), .reset(CLR));  // open: Qn, preset, en
  J_K_Flip_Flop j_k_ff_5 (.J(and_9_out), .clk(CLk), .K(and_10_out), .Q(Out[4]), .reset(CLR));  // open: Qn, preset, en
  J_K_Flip_Flop j_k_ff_6 (.J(and_11_out), .clk(CLk), .K(and_12_out), .Q(Out[5]), .reset(CLR));  // open: Qn, preset, en
  J_K_Flip_Flop j_k_ff_7 (.J(and_13_out), .clk(CLk), .K(and_14_out), .Q(Out[6]), .reset(CLR));  // open: Qn, preset, en
  J_K_Flip_Flop j_k_ff_8 (.J(and_15_out), .clk(CLk), .K(and_16_out), .Q(Out[7]), .reset(CLR));  // open: Qn, preset, en
  J_K_Flip_Flop j_k_ff_9 (.J(and_17_out), .clk(CLk), .K(and_18_out), .Q(Out[8]), .reset(CLR));  // open: Qn, preset, en
  J_K_Flip_Flop j_k_ff_10 (.J(and_19_out), .clk(CLk), .K(and_20_out), .Q(Out[9]), .reset(CLR));  // open: Qn, preset, en
  J_K_Flip_Flop j_k_ff_11 (
    .J(and_21_out), .clk(CLk), .K(and_22_out), .Q(Out[10]), .reset(CLR));  // open: Qn, preset, en
  J_K_Flip_Flop j_k_ff_12 (
    .J(and_23_out), .clk(CLk), .K(and_24_out), .Q(Out[11]), .reset(CLR));  // open: Qn, preset, en
  J_K_Flip_Flop j_k_ff_13 (
    .J(and_25_out), .clk(CLk), .K(and_26_out), .Q(Out[12]), .reset(CLR));  // open: Qn, preset, en
  J_K_Flip_Flop j_k_ff_14 (
    .J(and_27_out), .clk(CLk), .K(and_28_out), .Q(Out[13]), .reset(CLR));  // open: Qn, preset, en
  J_K_Flip_Flop j_k_ff_15 (
    .J(and_29_out), .clk(CLk), .K(and_30_out), .Q(Out[14]), .reset(CLR));  // open: Qn, preset, en
  J_K_Flip_Flop j_k_ff_16 (
    .J(and_31_out), .clk(CLk), .K(and_32_out), .Q(Out[15]), .reset(CLR));  // open: Qn, preset, en
  J_K_Flip_Flop j_k_ff_17 (
    .J(and_33_out), .clk(CLk), .K(and_34_out), .Q(Out[16]), .reset(CLR));  // open: Qn, preset, en
  J_K_Flip_Flop j_k_ff_18 (
    .J(and_35_out), .clk(CLk), .K(and_36_out), .Q(Out[17]), .reset(CLR));  // open: Qn, preset, en
  J_K_Flip_Flop j_k_ff_19 (
    .J(and_37_out), .clk(CLk), .K(and_38_out), .Q(Out[18]), .reset(CLR));  // open: Qn, preset, en
  J_K_Flip_Flop j_k_ff_20 (
    .J(and_39_out), .clk(CLk), .K(and_40_out), .Q(Out[19]), .reset(CLR));  // open: Qn, preset, en
  J_K_Flip_Flop j_k_ff_21 (
    .J(and_41_out), .clk(CLk), .K(and_42_out), .Q(Out[20]), .reset(CLR));  // open: Qn, preset, en
  J_K_Flip_Flop j_k_ff_22 (
    .J(and_43_out), .clk(CLk), .K(and_44_out), .Q(Out[21]), .reset(CLR));  // open: Qn, preset, en

  // Notes on the sheet:
  //   2207099
endmodule

module MBR (
  input  Counter,
  input  Load,
  input  [21:0] IN,
  input  CLK,
  input  CLR,
  output [21:0] OUT
);

  wire counter_load_4_bit_1_carry_out, counter_load_4_bit_2_carry_out, counter_load_4_bit_3_carry_out,
       counter_load_4_bit_4_carry_out, counter_load_4_bit_5_carry_out;

  Counter___Load_4_bit counter_load_4_bit_1 (
    .Cin(Counter), .Counter(Counter), .Load(Load), .I1(IN[0]), .I2(IN[1]), .I3(IN[2]), .I4(IN[3]),
    .A1(OUT[0]), .A2(OUT[1]), .A3(OUT[2]), .A4(OUT[3]), .Carry_Out(counter_load_4_bit_1_carry_out),
    .CLR(CLR), .CLK(CLK));
  Counter___Load_4_bit counter_load_4_bit_2 (
    .Cin(counter_load_4_bit_1_carry_out), .Counter(Counter), .Load(Load), .I1(IN[4]), .I2(IN[5]), .I3(IN[6]),
    .I4(IN[7]), .A1(OUT[4]), .A2(OUT[5]), .A3(OUT[6]), .A4(OUT[7]),
    .Carry_Out(counter_load_4_bit_2_carry_out), .CLR(CLR), .CLK(CLK));
  Counter___Load_4_bit counter_load_4_bit_3 (
    .Cin(counter_load_4_bit_2_carry_out), .Counter(Counter), .Load(Load), .I1(IN[8]), .I2(IN[9]),
    .I3(IN[10]), .I4(IN[11]), .A1(OUT[8]), .A2(OUT[9]), .A3(OUT[10]), .A4(OUT[11]),
    .Carry_Out(counter_load_4_bit_3_carry_out), .CLR(CLR), .CLK(CLK));
  Counter___Load_4_bit counter_load_4_bit_4 (
    .Cin(counter_load_4_bit_3_carry_out), .Counter(Counter), .Load(Load), .I1(IN[12]), .I2(IN[13]),
    .I3(IN[14]), .I4(IN[15]), .A1(OUT[12]), .A2(OUT[13]), .A3(OUT[14]), .A4(OUT[15]),
    .Carry_Out(counter_load_4_bit_4_carry_out), .CLR(CLR), .CLK(CLK));
  Counter___Load_4_bit counter_load_4_bit_5 (
    .Cin(counter_load_4_bit_4_carry_out), .Counter(Counter), .Load(Load), .I1(IN[16]), .I2(IN[17]),
    .I3(IN[18]), .I4(IN[19]), .A1(OUT[16]), .A2(OUT[17]), .A3(OUT[18]), .A4(OUT[19]),
    .Carry_Out(counter_load_4_bit_5_carry_out), .CLR(CLR), .CLK(CLK));
  CL_2_bit cl_2_bit_1 (
    .Cin(counter_load_4_bit_5_carry_out), .Counter(Counter), .Load(Load), .I1(IN[20]), .I2(IN[21]),
    .CLR(CLR), .A1(OUT[20]), .A2(OUT[21]), .CLK(CLK));  // open: Carry_Out
  // Probe on OUT

  // Other names for the same wires on the sheet: Count = Counter

  // Notes on the sheet:
  //   2207099
endmodule

module PC (
  input  Counter,
  input  Load,
  input  [4:0] IN,
  input  CLk,
  input  CLR,
  output [4:0] OUT
);

  wire and_1_out, and_2_out, and_3_out, and_4_out, counter_load_4_bit_1_carry_out, not_1_out, not_2_out,
       or_1_out, or_2_out;

  not not_1 (not_1_out, IN[4]);
  and and_1 (and_1_out, IN[4], Load);
  and and_2 (and_2_out, Load, not_1_out);
  not not_2 (not_2_out, Load);
  and and_3 (and_3_out, not_2_out, Counter);
  Counter___Load_4_bit counter_load_4_bit_1 (
    .Cin(Counter), .Counter(Counter), .Load(Load), .I1(IN[0]), .I2(IN[1]), .I3(IN[2]), .I4(IN[3]),
    .A1(OUT[0]), .A2(OUT[1]), .A3(OUT[2]), .A4(OUT[3]), .Carry_Out(counter_load_4_bit_1_carry_out),
    .CLR(CLR), .CLK(CLk));
  and and_4 (and_4_out, and_3_out, counter_load_4_bit_1_carry_out);
  or or_1 (or_1_out, and_1_out, and_4_out);
  or or_2 (or_2_out, and_4_out, and_2_out);
  J_K_Flip_Flop j_k_ff_1 (.J(or_1_out), .clk(CLk), .K(or_2_out), .Q(OUT[4]), .reset(CLR));  // open: Qn, preset, en
  // Probe on OUT

  // Other names for the same wires on the sheet: Count = Counter

  // Notes on the sheet:
  //   2207099
endmodule

module MAR (
  input  Load,
  input  [4:0] In,
  input  CLR,
  input  CLk,
  output [4:0] Out
);

  wire and_1_out, and_2_out, and_3_out, and_4_out, and_5_out, and_6_out, and_7_out, and_8_out, and_9_out,
       and_10_out, not_1_out, not_2_out, not_3_out, not_4_out, not_5_out;

  not not_1 (not_1_out, In[0]);
  not not_2 (not_2_out, In[1]);
  not not_3 (not_3_out, In[2]);
  not not_4 (not_4_out, In[3]);
  not not_5 (not_5_out, In[4]);
  and and_1 (and_1_out, In[0], Load);
  and and_2 (and_2_out, not_1_out, Load);
  and and_3 (and_3_out, In[1], Load);
  and and_4 (and_4_out, not_2_out, Load);
  and and_5 (and_5_out, In[2], Load);
  and and_6 (and_6_out, not_3_out, Load);
  and and_7 (and_7_out, In[3], Load);
  and and_8 (and_8_out, not_4_out, Load);
  and and_9 (and_9_out, In[4], Load);
  and and_10 (and_10_out, not_5_out, Load);
  J_K_Flip_Flop j_k_ff_1 (.J(and_1_out), .clk(CLk), .K(and_2_out), .Q(Out[0]), .reset(CLR));  // open: Qn, preset, en
  J_K_Flip_Flop j_k_ff_2 (.J(and_3_out), .clk(CLk), .K(and_4_out), .Q(Out[1]), .reset(CLR));  // open: Qn, preset, en
  J_K_Flip_Flop j_k_ff_3 (.J(and_5_out), .clk(CLk), .K(and_6_out), .Q(Out[2]), .reset(CLR));  // open: Qn, preset, en
  J_K_Flip_Flop j_k_ff_4 (.J(and_7_out), .clk(CLk), .K(and_8_out), .Q(Out[3]), .reset(CLR));  // open: Qn, preset, en
  J_K_Flip_Flop j_k_ff_5 (.J(and_9_out), .clk(CLk), .K(and_10_out), .Q(Out[4]), .reset(CLR));  // open: Qn, preset, en

  // Notes on the sheet:
  //   2207099
endmodule

module IR (
  input  Load,
  input  clk,
  input  [3:0] In,
  input  CLR,
  output [3:0] Out
);

  wire and_1_out, and_2_out, and_3_out, and_4_out, and_5_out, and_6_out, and_7_out, and_8_out, not_1_out,
       not_2_out, not_3_out, not_4_out;

  not not_1 (not_1_out, In[0]);
  not not_2 (not_2_out, In[1]);
  not not_3 (not_3_out, In[2]);
  not not_4 (not_4_out, In[3]);
  and and_1 (and_1_out, In[0], Load);
  and and_2 (and_2_out, not_1_out, Load);
  and and_3 (and_3_out, In[1], Load);
  and and_4 (and_4_out, not_2_out, Load);
  and and_5 (and_5_out, In[2], Load);
  and and_6 (and_6_out, not_3_out, Load);
  and and_7 (and_7_out, In[3], Load);
  and and_8 (and_8_out, not_4_out, Load);
  J_K_Flip_Flop j_k_ff_1 (.J(and_1_out), .clk(clk), .K(and_2_out), .Q(Out[0]), .reset(CLR));  // open: Qn, preset, en
  J_K_Flip_Flop j_k_ff_2 (.J(and_3_out), .clk(clk), .K(and_4_out), .Q(Out[1]), .reset(CLR));  // open: Qn, preset, en
  J_K_Flip_Flop j_k_ff_3 (.J(and_5_out), .clk(clk), .K(and_6_out), .Q(Out[2]), .reset(CLR));  // open: Qn, preset, en
  J_K_Flip_Flop j_k_ff_4 (.J(and_7_out), .clk(clk), .K(and_8_out), .Q(Out[3]), .reset(CLR));  // open: Qn, preset, en

  // Notes on the sheet:
  //   2207099
endmodule

module _2x1_MUX (
  input  [21:0] I0,
  input  [21:0] I1,
  input  S,
  output [21:0] O
);

  wire [21:0] and_1_out, and_2_out, bit_extender_1_out, not_1_out;

  assign not_1_out = ~bit_extender_1_out;  // NOT_Gate not_1, 22 bits wide
  assign and_1_out = I0 & not_1_out;  // AND_Gate and_1, 22 bits wide
  assign and_2_out = I1 & bit_extender_1_out;  // AND_Gate and_2, 22 bits wide
  assign bit_extender_1_out = {{21{1'b0}}, S};  // Bit_Extender bit_extender_1
  assign O = and_1_out | and_2_out;  // OR_Gate or_1, 22 bits wide

  // Notes on the sheet:
  //   2207099
endmodule

module Control_Unit (
  input  F,
  input  [3:0] IR,
  input  CLK,
  input  CLR,
  input  Bz,
  output R,
  output W,
  output a1,
  output a2,
  output a3,
  output b1,
  output b2,
  output b3,
  output c1,
  output c2,
  output d1,
  output d2,
  output I,
  output f1,
  output f2,
  output S,
  output a4,
  output inc_dec
);

  wire and_15_out, and_16_out, and_17_out, and_19_out, and_20_out, F_prime, or_1_out, or_2_out, or_3_out,
       or_4_out, or_5_out, or_7_out, or_8_out, or_9_out, or_11_out, or_12_out, q0, q1, q2, q3, q4, q5, q6,
       q8, q9, q10, q11, q12, q13, q14, q15, t0, t1, t2, t3;
  wire [1:0] g_register_1_out;

  or or_1 (or_1_out, q1, q9);
  or or_2 (or_2_out, or_3_out, q0, q1, q2, q3, q4, q6);
  and and_1 (f1, or_2_out, F_prime, t3);
  not not_1 (F_prime, F);
  or or_3 (or_3_out, q10, q11, q9, q8);
  Decoder #(.select(4), .enable("false")) decoder_1 (
    .out0(q0), .out1(q1), .out2(q2), .out3(q3), .out4(q4), .out5(q5), .out6(q6), .out7(S), .out8(q8),
    .out9(q9), .out10(q10), .out11(q11), .out12(q12), .out13(q13), .out14(q14), .out15(q15), .sel(IR));
  G_register g_register_1 (.CLK(CLK), .CLR(CLR), .OUT(g_register_1_out));
  and and_2 (a1, F, q0, t3);
  and and_3 (a2, F, or_1_out, t2);
  and and_4 (a3, F, q6, t3);
  Decoder #(.select(2), .enable("false")) decoder_2 (
    .out0(t0), .out1(t1), .out2(t2), .out3(t3), .sel(g_register_1_out));
  or or_4 (or_4_out, q2, inc_dec);
  and and_5 (b1, F, or_4_out, t2);
  and and_6 (b2, F, q3, t2);
  and and_7 (b3, F, q4, t2);
  and and_8 (c2, q5, t3);
  and and_9 (d1, F_prime, t0);
  and and_10 (d2, F, t0);
  and and_11 (f2, F, t3);
  and and_12 (I, F_prime, t2);
  and and_13 (a4, F, q8, t3);
  and and_14 (inc_dec, F, t2, or_5_out);
  or or_5 (or_5_out, q10, q11);
  and and_15 (and_15_out, F_prime, t1);
  and and_16 (and_16_out, q3, Bz);
  and and_17 (and_17_out, F_prime, t1);
  or or_6 (R, and_17_out, and_19_out);
  or or_7 (or_7_out, or_12_out, q2, q4, q3);
  and and_18 (W, or_7_out, F, t3);
  or or_8 (or_8_out, and_16_out, q4);
  or or_9 (or_9_out, q0, or_11_out, q1, q6, q3);
  and and_19 (and_19_out, or_9_out, F, t1);
  or or_10 (c1, and_15_out, and_20_out);
  and and_20 (and_20_out, or_8_out, F, t3);
  or or_11 (or_11_out, q10, q11, q9, q8);
  or or_12 (or_12_out, q10, q11);

  // Other names for the same wires on the sheet: q7 = S

  // Notes on the sheet:
  //   2207099
endmodule

module _4x1_MUX (
  input  [21:0] I0,
  input  [21:0] I1,
  input  [21:0] I0_2,
  input  [21:0] I1_2,
  input  [1:0] S,
  output [21:0] out
);

  wire [21:0] n2x1_mux_1_o, n2x1_mux_2_o;

  _2x1_MUX u_2x1_mux_1 (.I0(I0), .I1(I1), .S(S[0]), .O(n2x1_mux_1_o));
  _2x1_MUX u_2x1_mux_2 (.I0(I0_2), .I1(I1_2), .S(S[0]), .O(n2x1_mux_2_o));
  _2x1_MUX u_2x1_mux_3 (.I0(n2x1_mux_1_o), .I1(n2x1_mux_2_o), .S(S[1]), .O(out));

  // Notes on the sheet:
  //   2207099
endmodule

module G_register (
  input  CLK,
  input  CLR,
  output [1:0] OUT
);

  J_K_Flip_Flop j_k_ff_1 (.J(1'b1), .clk(CLK), .K(1'b1), .Q(OUT[0]), .reset(CLR));  // open: Qn, preset, en
  J_K_Flip_Flop j_k_ff_2 (.J(OUT[0]), .clk(CLK), .K(OUT[0]), .Q(OUT[1]), .reset(CLR));  // open: Qn, preset, en

  // Notes on the sheet:
  //   2207099
endmodule

module _2x1_MUX__5_bit (
  input  [4:0] I0,
  input  [4:0] I1,
  input  S,
  output [4:0] O
);

  wire [4:0] and_1_out, and_2_out, bit_extender_1_out, not_1_out;

  assign not_1_out = ~bit_extender_1_out;  // NOT_Gate not_1, 5 bits wide
  assign and_1_out = I0 & not_1_out;  // AND_Gate and_1, 5 bits wide
  assign and_2_out = I1 & bit_extender_1_out;  // AND_Gate and_2, 5 bits wide
  assign bit_extender_1_out = {{4{1'b0}}, S};  // Bit_Extender bit_extender_1
  assign O = and_1_out | and_2_out;  // OR_Gate or_1, 5 bits wide

  // Notes on the sheet:
  //   2207099
endmodule

module _16x1_MUX (
  input  [3:0] in_1,
  output [1:0] sbit
);

  wire [1:0] undriven, undriven_2;

  Multiplexer #(.select(4), .width(2), .enable("false")) multiplexer_1 (
    .in0(2'b10), .in1(2'b00), .in2(undriven), .in3(undriven), .in4(undriven), .in5(undriven), .in6(undriven),
    .in7(undriven), .in8(2'b11), .in9(2'b01), .in10(2'b00), .in11(2'b01), .in12(undriven_2),
    .in13(undriven_2), .in14(undriven_2), .in15(undriven_2), .out(sbit), .sel(in_1));

  // Notes on the sheet:
  //   2207099
endmodule

module _2x1_MUX__2_bit (
  input  [1:0] I0,
  input  [1:0] I1,
  input  S,
  output [1:0] O
);

  wire [1:0] and_1_out, and_2_out, bit_extender_1_out, not_1_out;

  assign not_1_out = ~bit_extender_1_out;  // NOT_Gate not_1, 2 bits wide
  assign and_1_out = I0 & not_1_out;  // AND_Gate and_1, 2 bits wide
  assign and_2_out = I1 & bit_extender_1_out;  // AND_Gate and_2, 2 bits wide
  assign bit_extender_1_out = {{1{1'b0}}, S};  // Bit_Extender bit_extender_1
  assign O = and_1_out | and_2_out;  // OR_Gate or_1, 2 bits wide

  // Notes on the sheet:
  //   2207099
endmodule
